# Fritzing sketch Diagram (saved by Fritzing 0.9.1b)
breadboards: 1

parts:
  Part1 = Arduino Uno (Rev3) - ICSP
  LED1 = smd LED [color="Red (633nm)" package="1206 [SMD]"]
  LED2 = smd LED [color="Red (633nm)" package="1206 [SMD]"]
  R1 = Resistor [package="0402 [SMD]"]
  R2 = Resistor [package="0402 [SMD]"]
  U1 = AD22100 - Voltage Output Temperature Sensor with Signal Conditioning [part_number=AD22100]

nets:
  N1: Part1.A0, U1.Vo
  N2: Part1.ICSP_MISO, Part1.D12/MISO, LED1.anode
  N3: Part1.D13/SCK, LED2.anode
  GND: Part1.GND, R1.Pin_0, R2.Pin_0, U1.GND
  N4: Part1.5V, U1.V+
  N5: LED1.cathode, R2.Pin_1
  N6: LED2.cathode, R1.Pin_1
